# Fritzing sketch Gateway (saved by Fritzing 0.9.3b)

parts:
  WeMos_D1_Mini1 = WeMos D1 Mini
  WeMos_D1_Mini2 = WeMos D1 Mini

nets:
  5V: WeMos_D1_Mini1.5V, WeMos_D1_Mini2.5V
  N1: WeMos_D1_Mini1.G, WeMos_D1_Mini2.G
  N2: WeMos_D1_Mini1.RST, WeMos_D1_Mini2.RST
  N3: WeMos_D1_Mini1.RX, WeMos_D1_Mini2.TX
  N4: WeMos_D1_Mini1.TX, WeMos_D1_Mini2.RX

notes:
  Serial
  Vcc
  Reset
  EnigmaIOT Gateway
  MQTT Bridge
