# Fritzing sketch Node (saved by Fritzing 0.9.3b)

parts:
  U1 = ESP8266 WiFi Module [part_number=ESP8266]
  BAT1 = Battery Holders [package=battery-aa]
  BAT2 = Battery Holders [package=battery-aa]
  U2 = TPS61200 [package=qfn-10_pad]
  C1 = Capacitor [part_number=10u package=cap-pth-small2]
  L1 = Inductors [part_number=2.2u package=npi75c]
  C3 = Capacitor [part_number=1u package=cap-pth-small2]
  R1 = Resistor [tolerance=±1% resistance=1.2M package="0603 [SMD]"]
  R2 = Resistor [tolerance=±1% resistance=220k package="0603 [SMD]"]
  R3 = Resistor [tolerance=±5% resistance=500k package="0603 [SMD]"]
  R4 = Resistor [tolerance=±1% resistance=250k package="0603 [SMD]"]
  C2 = Electrolytic Capacitor [capacitance=10µF package="200 mil [THT, electrolytic]"]
  C4 = Tantalum Capacitor [capacitance=1μF package="100 mil [THT, tantalum]"]
  JP1 = Header 4 [package=jst-4-pth]
  S1 = Momentary Switch [package=ksa_sealed_tac_switch]
  R5 = Resistor [tolerance=±1% resistance=10k package="0603 [SMD]"]
  R6 = Resistor [tolerance=±1% resistance=10k package="0603 [SMD]"]
  S2 = Momentary Switch [package=ksa_sealed_tac_switch]

nets:
  N1: U1.RXD, JP1.2
  N2: U1.VCC, U2.VOUT, R1.Pin_1, C2.+, C4.+, JP1.4, S1.2
  N3: U1.GPIO_0, S1.4
  GND: U1.GND, BAT1.-, BAT2.-, U2.PGND, U2.GND, U2.PAD, C1.1, C3.1, R2.Pin_0, R4.Pin_0, C2.-, C4.-, JP1.3, R5.Pin_0, R6.Pin_1
  N4: U1.TXD, JP1.1
  N5: U1.GPIO_15, R6.Pin_0
  N6: U1.REST, S2.1
  N7: BAT1.+, BAT2.+, U2.VIN, U2.EN, U2.PS, C1.2, L1.1, R3.Pin_1
  N8: U2.VAUX, C3.2
  N9: U2.L, L1.2
  N10: U2.UVLO, R3.Pin_0
  N11: U2.FB, R1.Pin_0, R2.Pin_1
  N12: S1.3, R5.Pin_1
